// Logisim project alu.circ as structural Verilog: 2 circuits, main circuit main
module main (
  input  [15:0] X,
  input  [15:0] Y,
  input  [5:0] switch__S,
  output signed_overflow,
  output [15:0] result,
  output equal
);

  wire comparator_1_lt;
  wire [3:0] shfty;
  wire [31:0] addR, and_1_out, bit_extender_1_out, or_1_out, shifter_1_out, shifter_2_out, shifter_3_out,
       subR, undriven, undriven_2, undriven_3, undriven_4, undriven_5;
  wire [31:16] multiplexer_1_out;

  // Probe on X
  // Probe on Y
  Comparator #(.width(16)) comparator_1 (.a(X), .b(Y), .eq(equal), .lt(comparator_1_lt));  // open: gt
  Shifter #(.width(16)) shifter_1 (.in(X), .\dist (shfty), .out(shifter_1_out[15:0]));
  Shifter #(.width(16), .shift("lr")) shifter_2 (.in(X), .\dist (shfty), .out(shifter_2_out[15:0]));
  Shifter #(.width(16), .shift("ar")) shifter_3 (.in(X), .\dist (shfty), .out(shifter_3_out[15:0]));
  Adder #(.width(16)) adder_1 (.a(X), .b(Y), .out(addR[15:0]));  // open: cin, cout
  Subtractor #(.width(16)) subtractor_1 (.a(X), .b(Y), .out(subR[15:0]));  // open: bin, bout
  assign and_1_out[15:0] = X & Y;  // AND_Gate and_1, 16 bits wide
  assign or_1_out[15:0] = X | Y;  // OR_Gate or_1, 16 bits wide
  // Probe on addR
  assign bit_extender_1_out[15:0] = {{15{1'b0}}, comparator_1_lt};  // Bit_Extender bit_extender_1
  Multiplexer #(.select(4), .width(32)) multiplexer_1 (
    .in0(and_1_out), .in1(or_1_out), .in2(bit_extender_1_out), .in3(shifter_1_out), .in4(shifter_2_out),
    .in5(shifter_3_out), .in6(addR), .in7(subR), .in8(undriven_2), .in9(undriven_3), .in10(undriven_5),
    .in11(undriven_4), .in12(undriven), .out({multiplexer_1_out, result}), .sel(switch__S[3:0]));  // open: in13, in14, in15, en
  // Probe on {multiplexer_1_out, result}
  BitSelector #(.width(16), .group(4)) bitselector_1 (.in(Y), .out(shfty), .sel(2'b00));
  overflow overflow_1 (
    .x(X), .y(Y), .addR(addR[15:0]), .subR(subR[15:0]), .rswitch(switch__S), .overflow(signed_overflow));
  // Pins of 4 and 6 bits meet at switch__S
  // Pins of 16 and 32 bits meet at and_1_out
  // Pins of 16 and 32 bits meet at shifter_1_out
  // Pins of 16 and 32 bits meet at {multiplexer_1_out, result}
  // Pins of 16 and 32 bits meet at shifter_3_out
  // Pins of 16 and 32 bits meet at bit_extender_1_out
  // Pins of 16 and 32 bits meet at addR
  // Pins of 16 and 32 bits meet at or_1_out
  // Pins of 16 and 32 bits meet at shifter_2_out
  // Pins of 16 and 32 bits meet at subR

  // Other names for the same wires on the sheet: oflow = signed_overflow; rswitch[5:0] = switch__S; shft[15:0] = Y;
  //   tunnel = equal

  // Notes on the sheet:
  //   8 - 
  //   9 -
  //   10 -
  //   11 -
  //   These are INPUTS to your circuit
  //   This is an INPUT to your circuit
  //   Legend
  //   0 - AND
  //   1 - OR
  //   2 - SLT
  //   3 - SLL
  //   4 - SRL
  //   5 - SRA
  //   6 - ADD
  //   7 - SUB
  //   12 - 
  //   13 - 
  //   DO NOT CHANGE THE LOCATIONS OF THE INPUTS/OUTPUTS! IF YOU DO SO, YOU NEED TO MAKE SURE THE PINS ARE AT THE RIGHT PLACE!
  //   These are OUTPUTS to your circuit
endmodule

module overflow (
  input  [15:0] x,
  input  [15:0] y,
  input  [15:0] addR,
  input  [15:0] subR,
  input  [5:0] rswitch,
  output overflow
);

  wire and_1_out, and_2_out, and_3_out, and_4_out, and_5_out, and_6_out, Azero, comparator_5_eq,
       comparator_6_eq, negAddR, negSubR, negX, negY, or_1_out, or_2_out, or_3_out, or_4_out, or_5_out,
       posAddR, posSubR, posX, posY, Szero;

  Comparator #(.width(16)) comparator_1 (.a(x), .b({16{1'b0}}), .gt(posX), .lt(negX));  // open: eq
  Comparator #(.width(16)) comparator_2 (.a(y), .b({16{1'b0}}), .gt(posY), .lt(negY));  // open: eq
  Comparator #(.width(16)) comparator_3 (.a(addR), .b({16{1'b0}}), .gt(posAddR), .eq(Azero), .lt(negAddR));
  Comparator #(.width(16)) comparator_4 (.a(subR), .b({16{1'b0}}), .gt(posSubR), .eq(Szero), .lt(negSubR));
  or or_1 (or_1_out, posAddR, Azero);
  or or_2 (or_2_out, negSubR, Szero);
  or or_3 (or_3_out, posSubR, Szero);
  and and_1 (and_1_out, posX, posY, negAddR);
  and and_2 (and_2_out, negX, negY, or_1_out);
  and and_3 (and_3_out, posX, negY, or_2_out);
  or or_4 (or_4_out, and_3_out, and_4_out);
  and and_4 (and_4_out, negX, posY, or_3_out);
  Comparator #(.width(6)) comparator_5 (.a(rswitch), .b(6'b000111), .eq(comparator_5_eq));  // open: gt, lt
  or or_5 (or_5_out, and_1_out, and_2_out);
  Comparator #(.width(6)) comparator_6 (.a(rswitch), .b(6'b000110), .eq(comparator_6_eq));  // open: gt, lt
  and and_5 (and_5_out, or_4_out, comparator_5_eq);
  and and_6 (and_6_out, or_5_out, comparator_6_eq);
  or or_6 (overflow, and_5_out, and_6_out);
endmodule
