// Logisim project cpu.circ as structural Verilog: 4 circuits, main circuit main
module main (
  input  [31:0] RS_READ_VALUE,
  input  [31:0] RT_READ_VALUE,
  input  [31:0] RD_READ_VALUE,
  input  [31:0] JC_READ_VALUE,
  input  [31:0] INSTRUCTION,
  input  CLOCK,
  input  RESET,
  output [4:0] RS,
  output [31:0] t0,
  output [31:0] t1,
  output [31:0] t2,
  output [31:0] t3,
  output [4:0] RI,
  output [4:0] RD,
  output [31:0] RD_WRITE_VALUE,
  output RD_WRITE_ENABLE,
  output [23:0] FETCH_ADDRESS
);

  wire i, j_test, jal;
  wire [1:0] result_mux;
  wire [2:0] u_dec_1_jc;
  wire [3:0] op, u_dec_1_out_2;
  wire [4:0] u_dec_1_rd;
  wire [16:0] Imm;
  wire [23:0] adder_1_out, multiplexer_3_out, multiplexer_4_out, u_dec_1_addr;
  wire [31:0] bit_extender_1_out, bit_extender_2_out, Data_Out, main_1_p2, Result;

  Multiplexer #(.width(5)) multiplexer_1 (.in0(u_dec_1_rd), .in1(5'b00110), .out(RD), .sel(jal));  // open: en
  u_DEC u_dec_1 (
    .in_1(INSTRUCTION), .out_2(u_dec_1_out_2), .JC(u_dec_1_jc), .RS(RS), .RI(RI), .RD(u_dec_1_rd),
    .Immi(Imm), .ADDR(u_dec_1_addr));  // open: I
  assign bit_extender_1_out = {{15{Imm[16]}}, Imm};  // Bit_Extender bit_extender_1
  // alu_main main_1: pin names not known; wires that end beside it: RS_READ_VALUE, main_1_p2, op, Result
  Multiplexer #(.width(32)) multiplexer_2 (
    .in0(RT_READ_VALUE), .in1(bit_extender_1_out), .out(main_1_p2), .sel(i));  // open: en
  u_CTRL u_ctrl_1 (
    .op(u_dec_1_out_2), .jc(u_dec_1_jc), .i(i), .jc_2(JC_READ_VALUE), .op_out(op), .result_mux(result_mux),
    .Mem_Write(RD_WRITE_ENABLE), .jal(jal), .j_test(j_test));  // open: access_byte, jc_out, i_out, access_byte_2
  Register #(.width(24)) register_1 (.D(multiplexer_3_out), .Q(FETCH_ADDRESS), .clk(CLOCK));  // open: en, clr
  Multiplexer #(.width(24)) multiplexer_3 (
    .in0(adder_1_out), .in1(multiplexer_4_out), .out(multiplexer_3_out), .sel(j_test));  // open: en
  // mem_main main_2: pin names not known; wires that end beside it: CLOCK, Data_Out
  Adder #(.width(24)) adder_1 (.a(24'h1), .b(FETCH_ADDRESS), .out(adder_1_out));  // open: cin, cout
  Multiplexer #(.width(24)) multiplexer_4 (
    .in0(RT_READ_VALUE[23:0]), .in1(u_dec_1_addr), .out(multiplexer_4_out), .sel(i));  // open: en
  assign bit_extender_2_out = {{8{1'b0}}, adder_1_out};  // Bit_Extender bit_extender_2
  Multiplexer #(.select(2), .width(32)) multiplexer_5 (
    .in0(Result), .in1(Data_Out), .in2(bit_extender_2_out), .out(RD_WRITE_VALUE), .sel(result_mux));  // open: in3, en

  // Other names for the same wires on the sheet: ADR_REG[31:0] = RT_READ_VALUE; CLK = CLOCK; jc[31:0] = JC_READ_VALUE;
  //   Write = RD_WRITE_ENABLE

  // Notes on the sheet:
  //   PC
  //   These are outputs to run.circ
  //   jump address
  //   address from reg
endmodule

module u_DEC (
  input  [31:0] in_1,
  output [3:0] out_2,
  output [2:0] JC,
  output I,
  output [4:0] RS,
  output [4:0] RI,
  output [4:0] RD,
  output [16:0] Immi,
  output [23:0] ADDR
);

  wire and_1_out;
  wire [2:0] demultiplexer_3_out0_2;
  wire [4:0] J_reg_RI, r_reg_RD, r_reg_RI, r_reg_RS;
  wire [16:5] demultiplexer_2_out0;
  wire [23:5] demultiplexer_3_out0;
  wire [26:17] demultiplexer_2_out1;
  wire [26:24] demultiplexer_3_out1;
  wire [27:0] demultiplexer_1_out0, demultiplexer_1_out1;

  and and_1 (and_1_out, in_1[28], in_1[29], in_1[30], in_1[31]);
  Demultiplexer #(.width(28)) demultiplexer_1 (
    .out0(demultiplexer_1_out0), .out1(demultiplexer_1_out1), .in(in_1[27:0]), .sel(and_1_out));  // open: en
  Demultiplexer #(.width(27)) demultiplexer_2 (
    .out0({r_reg_RD, r_reg_RS, demultiplexer_2_out0, r_reg_RI}), .out1({demultiplexer_2_out1, Immi}),
    .in(demultiplexer_1_out0[26:0]), .sel(demultiplexer_1_out0[27]));  // open: en
  Demultiplexer #(.width(27)) demultiplexer_3 (
    .out0({demultiplexer_3_out0_2, demultiplexer_3_out0, J_reg_RI}), .out1({demultiplexer_3_out1, ADDR}),
    .in(demultiplexer_1_out1[26:0]), .sel(demultiplexer_1_out1[27]));  // open: en
  Multiplexer #(.width(5)) multiplexer_1 (
    .in0(r_reg_RS), .in1(demultiplexer_2_out1[21:17]), .out(RS), .sel(demultiplexer_1_out0[27]));  // open: en
  Multiplexer #(.width(5)) multiplexer_2 (
    .in0(r_reg_RD), .in1(demultiplexer_2_out1[26:22]), .out(RD), .sel(demultiplexer_1_out0[27]));  // open: en
  Multiplexer #(.width(5)) multiplexer_3 (.in0(r_reg_RI), .in1(J_reg_RI), .out(RI), .sel(and_1_out));  // open: en
  Multiplexer #(.width(3)) multiplexer_4 (
    .in0(demultiplexer_3_out0_2), .in1(demultiplexer_3_out1), .out(JC), .sel(demultiplexer_1_out1[27]));  // open: en
  Multiplexer multiplexer_5 (
    .in0(demultiplexer_1_out0[27]), .in1(demultiplexer_1_out1[27]), .out(I), .sel(and_1_out));  // open: en

  assign out_2 = in_1[31:28];

  // Other names for the same wires on the sheet: imm[16:0] = Immi; op[3:0] = in_1[31:28]

  // Notes on the sheet:
  //   check for J type
  //   $RI
  //   $RS
  //   $RD
  //   r-type
  //   j-type
  //   $RI
  //   JC
  //   from reg
  //   from reg
  //   from immi
  //   from addr
  //   immi
  //   $RS
  //   $RD
  //   addr
  //   JC
endmodule

module u_CTRL (
  input  [3:0] op,
  input  [2:0] jc,
  input  i,
  input  [31:0] jc_2,
  output access_byte,
  output [3:0] op_out,
  output [2:0] jc_out,
  output i_out,
  output access_byte_2,
  output [1:0] result_mux,
  output Mem_Write,
  output jal,
  output j_test
);

  wire and_2_out, comparator_1_eq, comparator_2_lt, comparator_3_gt, comparator_4_lt, comparator_5_eq,
       comparator_6_eq, comparator_7_eq, comparator_8_eq, comparator_9_eq, comparator_10_eq,
       comparator_11_eq, comparator_12_eq, comparator_13_eq, comparator_14_eq, comparator_15_eq, or_1_out,
       or_2_out, or_4_out, u_jumpcomp_1_jc_passed;
  wire [1:0] adder_1_out, bit_extender_1_out, bit_extender_2_out, bit_extender_3_out, bit_extender_4_out,
       subtractor_1_out;

  Comparator #(.width(4), .mode("unsigned")) comparator_1 (.a(op), .b(4'b1111), .eq(comparator_1_eq));  // open: gt, lt
  u_JumpComp u_jumpcomp_1 (.jc(jc_2), .jc_2(jc), .jc_passed(u_jumpcomp_1_jc_passed));
  Comparator #(.width(4), .mode("unsigned")) comparator_2 (.a(op), .b(4'b1011), .lt(comparator_2_lt));  // open: gt, eq
  Comparator #(.width(4), .mode("unsigned")) comparator_3 (.a(op), .b(4'b1001), .gt(comparator_3_gt));  // open: eq, lt
  Comparator #(.width(4), .mode("unsigned")) comparator_4 (.a(op), .b(4'b1111), .lt(comparator_4_lt));  // open: gt, eq
  Comparator #(.width(4), .mode("unsigned")) comparator_5 (.a(op), .b(4'b1111), .eq(comparator_5_eq));  // open: gt, lt
  Comparator #(.width(3), .mode("unsigned")) comparator_6 (.a(jc), .b(3'b111), .eq(comparator_6_eq));  // open: gt, lt
  Comparator #(.width(4), .mode("unsigned")) comparator_7 (.a(op), .b(4'b1100), .eq(comparator_7_eq));  // open: gt, lt
  Comparator #(.width(4), .mode("unsigned")) comparator_8 (.a(op), .b(4'b1110), .eq(comparator_8_eq));  // open: gt, lt
  Comparator #(.width(4), .mode("unsigned")) comparator_9 (.a(op), .b(4'b1111), .eq(comparator_9_eq));  // open: gt, lt
  or or_1 (or_1_out, comparator_2_lt, comparator_6_eq);
  or or_2 (or_2_out, comparator_7_eq, comparator_8_eq);
  and and_1 (j_test, comparator_1_eq, u_jumpcomp_1_jc_passed);
  and and_2 (and_2_out, comparator_3_gt, comparator_4_lt);
  Comparator #(.width(4), .mode("unsigned")) comparator_10 (
    .a(4'b1101), .b(op), .eq(comparator_10_eq));  // open: gt, lt
  Comparator #(.width(4), .mode("unsigned")) comparator_11 (
    .a(4'b1100), .b(op), .eq(comparator_11_eq));  // open: gt, lt
  assign bit_extender_1_out = {{1{1'b0}}, and_2_out};  // Bit_Extender bit_extender_1
  Adder #(.width(2)) adder_1 (.a(bit_extender_1_out), .b(bit_extender_2_out), .out(adder_1_out));  // open: cin, cout
  assign bit_extender_2_out = {{1{1'b0}}, comparator_5_eq};  // Bit_Extender bit_extender_2
  and and_3 (jal, comparator_9_eq, comparator_6_eq);
  Comparator #(.width(4), .mode("unsigned")) comparator_12 (
    .a(op), .b(4'b1101), .eq(comparator_12_eq));  // open: gt, lt
  or or_3 (access_byte, comparator_10_eq, comparator_11_eq);
  Comparator #(.width(4), .mode("unsigned")) comparator_13 (
    .a(4'b1101), .b(op), .eq(comparator_13_eq));  // open: gt, lt
  Comparator #(.width(4), .mode("unsigned")) comparator_14 (
    .a(4'b1011), .b(op), .eq(comparator_14_eq));  // open: gt, lt
  Comparator #(.width(4), .mode("unsigned")) comparator_15 (
    .a(op), .b(4'b1110), .eq(comparator_15_eq));  // open: gt, lt
  or or_4 (or_4_out, or_1_out, or_2_out);
  or or_5 (access_byte_2, comparator_13_eq, comparator_14_eq);
  Subtractor #(.width(2)) subtractor_1 (
    .a(adder_1_out), .b(bit_extender_3_out), .out(subtractor_1_out));  // open: bin, bout
  assign bit_extender_3_out = {{1{1'b0}}, comparator_15_eq};  // Bit_Extender bit_extender_3
  assign bit_extender_4_out = {{1{1'b0}}, jal};  // Bit_Extender bit_extender_4
  or or_6 (Mem_Write, or_4_out, comparator_12_eq);
  Adder #(.width(2)) adder_2 (.a(subtractor_1_out), .b(bit_extender_4_out), .out(result_mux));  // open: cin, cout

  assign i_out = i;
  assign jc_out = jc;
  assign op_out = op;
endmodule

module u_JumpComp (
  input  [31:0] jc,
  input  [2:0] jc_2,
  output jc_passed
);

  wire comparator_1_eq, comparator_1_gt, comparator_1_lt, or_1_out, or_2_out, or_3_out;

  Comparator #(.width(32)) comparator_1 (
    .a(jc), .b({32{1'b0}}), .gt(comparator_1_gt), .eq(comparator_1_eq), .lt(comparator_1_lt));
  or or_1 (or_1_out, comparator_1_eq, comparator_1_lt);
  or or_2 (or_2_out, comparator_1_gt, comparator_1_lt);
  or or_3 (or_3_out, comparator_1_eq, comparator_1_gt);
  Multiplexer #(.select(3)) multiplexer_1 (
    .in0(1'b1), .in1(comparator_1_gt), .in2(comparator_1_eq), .in3(comparator_1_lt), .in4(or_1_out),
    .in5(or_2_out), .in6(or_3_out), .in7(1'b1), .out(jc_passed), .sel(jc_2));  // open: en
endmodule
